# Fritzing sketch door_security_system (saved by Fritzing 0.9.3b)

parts:
  +_BUZZER = Piezo Speaker
  G = LED - 5mm [color="Red (633nm)" package="5 mm [THT]"]
  R = LED - 5mm [color="Red (633nm)" package="5 mm [THT]"]
  SWITCH_+ = Toggle Switch [package=THT]
  3_3v = RFID-RC522-v2
  DOOR-SECURITY-SYSTEM_1_0 = Arduino Nano (Rev3.0)
  R1 = Resistor [tolerance=±5% resistance=220 package=THT]
  REED_g = KY-021 Mini Magnetic Reed Switch Module [package="Breakout board"]
  POWER_+ = female pin header, 2 pins [form="♀ (female)"]
  MOTOR_+ = DC Motor  # not connected

nets:
  GND: +_BUZZER.pin1, SWITCH_+.COM, 3_3v.GND, DOOR-SECURITY-SYSTEM_1_0.GND, R1.Pin_1, REED_g.-, POWER_+.pin1
  N1: +_BUZZER.pin2, DOOR-SECURITY-SYSTEM_1_0.D9
  N2: G.cathode, R.cathode, R1.Pin_0
  N3: G.anode, DOOR-SECURITY-SYSTEM_1_0.D3
  N4: R.anode, DOOR-SECURITY-SYSTEM_1_0.D4
  N5: SWITCH_+.L1, DOOR-SECURITY-SYSTEM_1_0.D6
  N6: 3_3v.SDA, DOOR-SECURITY-SYSTEM_1_0.D10
  N7: 3_3v.SCK, DOOR-SECURITY-SYSTEM_1_0.D13/SCK
  N8: 3_3v.MOSI, DOOR-SECURITY-SYSTEM_1_0.D11/MOSI
  N9: 3_3v.MISO, DOOR-SECURITY-SYSTEM_1_0.D12/MISO
  N10: 3_3v.RST, DOOR-SECURITY-SYSTEM_1_0.D8
  3.3V: 3_3v.3.3V, DOOR-SECURITY-SYSTEM_1_0.3V3
  N11: DOOR-SECURITY-SYSTEM_1_0.D7, REED_g.S
  N12: DOOR-SECURITY-SYSTEM_1_0.VIN, POWER_+.pin2
  5V: DOOR-SECURITY-SYSTEM_1_0.5V, REED_g.Vin

custom parts:
  RFID-RC522-v2: A simple China made RFID-RC522 Reader; do check the pin labels, as this is a MFRC522 based clone.
  KY-021 Mini Magnetic Reed Switch Module: KY-021 magnetic reed switch module. A reed switch is a magnetic sensor that is normally open and gets closed when exposed to a magnetic field.
